# Fritzing sketch Circuit Schematic (saved by Fritzing 0.9.3b)
breadboards: 1

parts:
  Part2 = Arduino Uno (Rev3) - ICSP
  J1 = Basic Servo
  P1 = S1133 Si Photodiode [package="8mm Ceramic [THT]"]
  P2 = S1133 Si Photodiode [package="8mm Ceramic [THT]"]
  R1 = Resistor [tolerance=±5% resistance=10k package="2512 [SMD]"]
  R2 = Resistor [tolerance=±5% resistance=10k package="2512 [SMD]"]

nets:
  N1: Part2.A0, P2.cathode, R1.Pin_1
  N2: Part2.A1, P1.cathode, R2.Pin_0
  N3: Part2.D2, J1.pulse
  5V: Part2.5V, J1.vcc, P2.anode
  GND: Part2.GND, J1.gnd, P1.anode, R1.Pin_0, R2.Pin_1
